# Fritzing sketch connections (saved by Fritzing 0.9.5d)

parts:
  Raspberry_Pi_1 = Raspberry Pi 3 [part_number=RPI-3-V1.2]
  R1 = Resistor [tolerance=±5% resistance=220 package=THT]
  LED1 = smd LED [color="Red (633nm)" package="1206 [SMD]"]
  LED2 = smd LED [color="Yellow (595nm)" package="1206 [SMD]"]
  LED3 = smd LED [color="Green (560nm)" package="1206 [SMD]"]
  R2 = Resistor [tolerance=±5% resistance=220 package=THT]
  R3 = Resistor [tolerance=±5% resistance=220 package=THT]
  S1 = Momentary Switch [package=ksa_sealed_tac_switch]
  S2 = Momentary Switch [package=ksa_sealed_tac_switch]

nets:
  N1: Raspberry_Pi_1.GND, LED1.cathode, LED2.cathode, LED3.cathode, S1.1, S2.1
  N2: Raspberry_Pi_1.GIPO5, S1.3
  N3: Raspberry_Pi_1.GIPO6, S2.3
  N4: Raspberry_Pi_1.GIPO13, R1.Pin_1
  N5: Raspberry_Pi_1.GIPO19, R2.Pin_1
  N6: Raspberry_Pi_1.GIPO26, R3.Pin_1
  N7: R1.Pin_0, LED3.anode
  N8: LED1.anode, R2.Pin_0
  N9: LED2.anode, R3.Pin_0
